# Fritzing sketch Circuit diagram (saved by Fritzing 0.8.7b)
breadboards: 1

parts:
  Raspberry_Pi_1 = Raspberry Pi 3
  Part1 = SRF05 Ultrasonic Rangefinder
  S1 = Pushbutton [package="[THT]"]
  LED1 = LED - 5mm [color="Red (633nm)" package="5 mm [THT]"]
  LED2 = LED - 5mm [color="Red (633nm)" package="5 mm [THT]"]
  IC1 = Rasberry Pi NIOR Camera [chip_label=IC package="DIP (Dual Inline) [THT]"]  # not connected
  R1 = Resistor [tolerance=±5% resistance=220 package=THT]
  R2 = Resistor [tolerance=±5% resistance=220 package=THT]
  R3 = Resistor [tolerance=±5% resistance=220 package=THT]

nets:
  N1: Raspberry_Pi_1.GIPO21, Raspberry_Pi_1.GIPO16, S1.Pin_1, S1.Pin_2, R3.Pin_0
  N2: Raspberry_Pi_1.GIPO20, R2.Pin_0
  GND: Raspberry_Pi_1.GND, Part1.GND, LED1.cathode, LED2.cathode, R3.Pin_1
  N3: Raspberry_Pi_1.GIPO23, R1.Pin_0
  N4: Raspberry_Pi_1.GIPO18, Part1.Trig
  N5: Raspberry_Pi_1.GIPO15, Part1.Echo
  5V: Raspberry_Pi_1.5V, Part1.VCC, S1.Pin_3, S1.Pin_4
  N6: LED1.anode, R1.Pin_1
  N7: LED2.anode, R2.Pin_1

custom parts:
  Rasberry Pi NIOR Camera: Camera
